# Fritzing sketch shifty-circuit (saved by Fritzing 0.9.2b)
breadboards: 1

parts:
  Bauteil1 = Arduino Uno (Rev3) - ICSP
  U1 = ESP8266 WiFi Module [part_number=ESP8266]
  J1 = Piezo Speaker
  S1 = Toggle Switch [package=THT]  # not connected
  LED2 = smd LED [color="Green (570nm)" package="0805 [SMD]"]
  C5 = Ceramic Capacitor [capacitance=0.1µF package="1206 [SMD, multilayer]"]
  R3 = Resistor [tolerance=±0.5% resistance=220 package=THT]
  R4 = Resistor [tolerance=±0.5% resistance=220 package=THT]  # not connected
  R5 = Resistor [tolerance=±0.5% resistance=220 package=THT]
  R6 = Resistor [tolerance=±0.5% resistance=220 package=THT]
  R7 = Resistor [tolerance=±0.5% resistance=1M package=THT]
  C6 = Ceramic Capacitor [capacitance=100nF package="200 mil [THT, multilayer]"]

nets:
  N1: Bauteil1.D2, R7.Pin_0, C6.0
  N2: Bauteil1.D3_PWM, R6.Pin_0
  N3: Bauteil1.D4, J1.pin2
  N4: Bauteil1.D7, U1.TXD
  3V3: Bauteil1.3V3, U1.VCC, U1.RST, U1.CH_PD, C5.0
  GND: Bauteil1.GND, U1.GND, J1.pin1, C5.1, R5.Pin_1, R7.Pin_1, C6.1
  N5: U1.RXD, R3.Pin_1
  N6: LED2.anode, R6.Pin_1

notes:
  Ground connected with cable shields
  Button +
  Button -
  This sketch shows the assignment of the Arduino pins. However, these are accessed through stacking headers of the attached Adafruit MotorShield v2.3.
  This MotorShield has a power + and - connection (with On/Off switch, approx. 10.6V), the set jumper and the 4 motor cables at port M3 and M4.
  These 4 motor cables and the additional 3 outgoing cables in this sketch go to the shielded cable harnesses.
  10.6V Power + and - (with switch in front)
  The motor cables coming from the MotorShield in M3 and M4

custom parts:
  ESP8266 WiFi Module: Generic WiFi Module based on the ESP8266 with onboard PCB antenna and UART communications
